// Logisim project MCU.circ as structural Verilog
module MCU (
  input  [4:0] KBD_command,
  input  [10:0] KBD_energy_increment,
  input  KBD_Ready,
  input  Reset,
  input  CLK,
  input  MISO,
  input  SPI_busy,
  output Request_KBD,
  output Request_KBD_energy,
  output [7:0] Cell_CSC,
  output [7:0] Cell_CSR,
  output [2:0] Table_CSC,
  output [5:0] Table_CSR,
  output Task_CS,
  output SPI_clock,
  output MOSI,
  output [7:0] Debug_out,
  output Waiting_IO,
  output SPI_communication_in_progress
);

  wire and_1_out, and_2_out, and_3_out, and_4_out, and_5_out, and_6_out, and_7_out, and_8_out, and_10_out,
       and_11_out, cdm_8_1_data_code_prime, cdm_8_1_load_st_prime, cdm_8_1_mem, d_ff_1_q, Data,
       decoder_1_out0, io_dmx_1_cell_csc, io_dmx_1_cell_csr, io_dmx_1_debug_output, io_dmx_1_is_io,
       io_dmx_1_spi_kbd_control, io_dmx_1_table__csc__csr____task_cs, io_dmx_1_universal_io_1,
       io_dmx_1_universal_io_2, not_1_out, or_1_out, or_2_out, or_3_out, or_5_out,
       spi_module_master_1_communication_end, spi_module_master_1_input_transanction_end,
       spi_module_master_1_output_transanction_end;
  wire [6:0] demultiplexer_2_out0, demultiplexer_2_out1, register_4_q;
  wire [6:3] register_3_q;
  wire [7:0] cdm_8_1_addr, cdm_8_1_data_out, cdm_8_1_pc, cdm_8_1_ps, cdm_8_1_r0, cdm_8_1_r1, cdm_8_1_r2,
       cdm_8_1_r3, cdm_8_1_sp, controlled_buffer_1_out, controlled_buffer_2_out, controlled_buffer_4_out,
       controlled_buffer_6_out, register_5_q, register_6_q;
  wire [15:0] spi_module_master_1_recv_data;

  // Probe on cdm_8_1_r0
  // Probe on cdm_8_1_r0
  // Probe on cdm_8_1_r0
  // Probe on cdm_8_1_ps[6:4]
  // Probe on cdm_8_1_ps[7]
  // Probe on cdm_8_1_pc
  // Probe on cdm_8_1_r1
  // Probe on cdm_8_1_r0
  // Probe on cdm_8_1_ps[2]
  // Probe on cdm_8_1_ps[3]
  // Probe on cdm_8_1_r1
  // Probe on cdm_8_1_r1
  // Probe on cdm_8_1_r1
  // Probe on cdm_8_1_ps[0]
  // Probe on cdm_8_1_ps[1]
  // Probe on cdm_8_1_r2
  // Probe on cdm_8_1_r2
  // Probe on cdm_8_1_r2
  // Probe on cdm_8_1_r2
  // Probe on cdm_8_1_sp
  // Probe on cdm_8_1_r3
  // Probe on cdm_8_1_r3
  and and_1 (and_1_out, CLK, ~Waiting_IO);  // AND_Gate
  // Probe on cdm_8_1_r3
  // Probe on cdm_8_1_r3
  CdM_8 cdm_8_1 (
    .data_code_prime(cdm_8_1_data_code_prime), .R0(cdm_8_1_r0), .R1(cdm_8_1_r1), .mem(cdm_8_1_mem),
    .R2(cdm_8_1_r2), .load_st_prime(cdm_8_1_load_st_prime), .R3(cdm_8_1_r3), .addr(cdm_8_1_addr),
    .PC(cdm_8_1_pc), .SP(cdm_8_1_sp), .data_out(cdm_8_1_data_out), .data_in(controlled_buffer_2_out),
    .PS(cdm_8_1_ps), .clk(and_1_out), .rset(Reset));  // open: page, IAck, IRQ, vector, shadow
  Decoder #(.disabled(0)) decoder_1 (
    .out0(decoder_1_out0), .out1(Data), .sel(cdm_8_1_data_code_prime), .en(cdm_8_1_mem));
  assign controlled_buffer_1_out = not_1_out ? cdm_8_1_data_out : 8'bz;  // Controlled_Buffer controlled_buffer_1
  not not_1 (not_1_out, cdm_8_1_load_st_prime);
  assign controlled_buffer_2_out = cdm_8_1_load_st_prime ? controlled_buffer_1_out : 8'bz;  // Controlled_Buffer controlled_buffer_2
  and and_2 (and_2_out, ~io_dmx_1_is_io, Data);  // AND_Gate
  IO_dmx io_dmx_1 (
    .Address(cdm_8_1_addr), .Is_IO(io_dmx_1_is_io), .Cell_CSC(io_dmx_1_cell_csc),
    .Cell_CSR(io_dmx_1_cell_csr), .Table__CSC__CSR____Task_CS(io_dmx_1_table__csc__csr____task_cs),
    .SPI_KBD_control(io_dmx_1_spi_kbd_control), .Universal_IO_1(io_dmx_1_universal_io_1),
    .Universal_IO_2(io_dmx_1_universal_io_2), .Debug_output(io_dmx_1_debug_output), .Selected(Data));
  ROM rom_1 (.addr(cdm_8_1_addr), .data(controlled_buffer_1_out), .sel(decoder_1_out0));
  RAM ram_1 (
    .addr(cdm_8_1_addr), .data(controlled_buffer_1_out), .sel(and_2_out), .clk(CLK),
    .ld(cdm_8_1_load_st_prime), .clr(Reset));
  and and_3 (and_3_out, io_dmx_1_is_io, ~cdm_8_1_load_st_prime, io_dmx_1_universal_io_1);  // AND_Gate
  or or_1 (or_1_out, io_dmx_1_universal_io_1, spi_module_master_1_communication_end, and_11_out);
  and and_4 (and_4_out, io_dmx_1_is_io, ~cdm_8_1_load_st_prime, io_dmx_1_universal_io_2);  // AND_Gate
  or or_2 (or_2_out, io_dmx_1_universal_io_2, spi_module_master_1_communication_end, and_11_out);
  Register #(.trigger("falling")) register_1 (
    .D(controlled_buffer_1_out), .en(io_dmx_1_cell_csc), .Q(Cell_CSC), .clk(CLK), .clr(Reset));
  Register #(.trigger("falling")) register_2 (
    .D(controlled_buffer_1_out), .en(io_dmx_1_cell_csr), .Q(Cell_CSR), .clk(CLK), .clr(Reset));
  Register #(.trigger("falling")) register_3 (
    .D(controlled_buffer_1_out), .en(io_dmx_1_table__csc__csr____task_cs),
    .Q({Task_CS, register_3_q, Table_CSC}), .clk(CLK), .clr(Reset));
  Register #(.trigger("falling")) register_4 (
    .D(controlled_buffer_1_out), .en(io_dmx_1_spi_kbd_control), .Q({Request_KBD, register_4_q}), .clk(CLK),
    .clr(or_3_out));
  and and_5 (and_5_out, io_dmx_1_is_io, cdm_8_1_load_st_prime, io_dmx_1_universal_io_1);
  assign controlled_buffer_1_out = and_5_out ? register_5_q : 8'bz;  // Controlled_Buffer controlled_buffer_3
  Register #(.trigger("falling")) register_5 (
    .D(controlled_buffer_4_out), .en(or_1_out), .Q(register_5_q), .clk(CLK), .clr(Reset));
  assign controlled_buffer_4_out = and_3_out ? controlled_buffer_1_out : 8'bz;  // Controlled_Buffer controlled_buffer_4
  and and_6 (and_6_out, io_dmx_1_is_io, io_dmx_1_universal_io_2, cdm_8_1_load_st_prime);
  assign controlled_buffer_1_out = and_6_out ? register_6_q : 8'bz;  // Controlled_Buffer controlled_buffer_5
  Register #(.trigger("falling")) register_6 (
    .D(controlled_buffer_6_out), .en(or_2_out), .Q(register_6_q), .clk(CLK), .clr(Reset));
  assign controlled_buffer_6_out = and_4_out ? controlled_buffer_1_out : 8'bz;  // Controlled_Buffer controlled_buffer_6
  Register #(.trigger("falling")) register_7 (
    .D(controlled_buffer_1_out), .en(io_dmx_1_debug_output), .Q(Debug_out), .clk(CLK), .clr(Reset));
  Demultiplexer #(.width(3), .disabled(0), .enable("false")) demultiplexer_1 (
    .out0(Table_CSR[2:0]), .out1(Table_CSR[5:3]), .in(register_3_q[5:3]), .sel(register_3_q[6]));
  Demultiplexer #(.width(7), .disabled(0), .enable("false")) demultiplexer_2 (
    .out0(demultiplexer_2_out0), .out1(demultiplexer_2_out1), .in(register_4_q), .sel(Request_KBD));
  or or_3 (or_3_out, and_7_out, Reset);
  and and_7 (and_7_out, Waiting_IO, or_5_out, and_8_out);
  D_Flip_Flop d_ff_1 (.clk(CLK), .D(CLK), .Q(d_ff_1_q), .reset(and_8_out));  // open: Qn, preset, en
  or or_4 (Waiting_IO, Request_KBD, SPI_communication_in_progress);
  or or_5 (or_5_out, and_11_out, spi_module_master_1_communication_end);
  and and_8 (and_8_out, ~CLK, d_ff_1_q);  // AND_Gate
  or or_6 (SPI_communication_in_progress, demultiplexer_2_out0[6], demultiplexer_2_out0[5], demultiplexer_2_out0[4], demultiplexer_2_out0[3], demultiplexer_2_out0[2], demultiplexer_2_out0[1], demultiplexer_2_out0[0]);
  and and_9 (Request_KBD_energy, demultiplexer_2_out1[0], Request_KBD);
  Pull_Resistor pull_resistor_1 (.node(SPI_busy));
  assign {controlled_buffer_6_out, controlled_buffer_4_out} = and_11_out ? {KBD_energy_increment, KBD_command} : 16'bz;  // Controlled_Buffer controlled_buffer_7
  assign {controlled_buffer_6_out, controlled_buffer_4_out} = spi_module_master_1_communication_end ? spi_module_master_1_recv_data : 16'bz;  // Controlled_Buffer controlled_buffer_8
  and and_10 (and_10_out, CLK, SPI_communication_in_progress, ~SPI_busy);  // AND_Gate
  LED led_1 (.in(spi_module_master_1_input_transanction_end));
  SPI_module__master spi_module_master_1 (
    .In_clock(and_10_out), .MISO(MISO), .CLK(SPI_clock), .MOSI(MOSI),
    .Output_transanction_end(spi_module_master_1_output_transanction_end),
    .Input_transanction_end(spi_module_master_1_input_transanction_end),
    .Control_command({Request_KBD, register_4_q}), .Send_command(register_5_q[4:0]),
    .Send_energy({register_6_q, register_5_q[7:5]}), .Recv_data(spi_module_master_1_recv_data),
    .Communication_end(spi_module_master_1_communication_end));
  LED led_2 (.in(spi_module_master_1_communication_end));
  LED led_3 (.in(spi_module_master_1_output_transanction_end));
  and and_11 (and_11_out, Request_KBD, KBD_Ready);
  Pull_Resistor pull_resistor_2 (.node(MISO));

  // Other names for the same wires on the sheet: wait_KBD = Request_KBD; wait_IO = Waiting_IO;
  //   wait_SPI = SPI_communication_in_progress

  // Notes on the sheet:
  //   contents of rom_1 (hex, n*v repeats v):
  //   d0 f9 d1 ff a1 d0 ff d1 ff a1 88 a1 d0 fc d1 2e a1 d0 fb d1 10 a1 d0 fc d1 c a1 d0 f9 d1 0 a1 d0 ff
  //   d1 0 a1 88 a1 d0 ea d1 1 a1 d2 ff a9 88 a1 8a a9 d0 fc d1 26 a1 d0 fc d1 80 a1 d0 fb b1 d0 10 71 e1
  //   55 0 d0 f9 d1 18 a1 d0 e9 b1 9d a1 d0 fe a1 ee 33 d0 11 71 e1 6a 0 d0 f9 d1 3 a1 d0 ea b1 9d a1 d0
  //   ff a1 ee 33 d0 12 71 e1 82 0 d0 f9 d1 c0 a1 d0 ea b1 91 e3 7c 91 a1 d0 ff a1 ee 33 d0 13 71 e1 9a 0
  //   d0 f9 d1 24 a1 d0 e9 b1 91 e3 94 91 a1 d0 fe a1 ee 33 d0 8 71 e1 d7 d0 ff d1 0 a1 d2 ea b9 a1 d0 fc
  //   d1 2e a1 d0 f9 d1 42 a1 d0 fc d1 81 a1 d0 fb b1 d2 8 56 a2 d0 fc d1 4 a1 d0 fb b1 d0 f9 d2 d0 56 a2
  //   d0 ff d1 0 a1 d2 ea b9 a1 ee 33 d0 f9 d1 c3 a1 d1 0 d0 ff a1 d0 ea b1 d0 ff a1 ee 33
endmodule

module IO_dmx (
  input  [7:0] Address,
  input  Selected,
  output Is_IO,
  output Cell_CSC,
  output Cell_CSR,
  output Table__CSC__CSR____Task_CS,
  output SPI_KBD_control,
  output Universal_IO_1,
  output Universal_IO_2,
  output Debug_output
);

  wire [7:0] controlled_buffer_1_out;

  assign controlled_buffer_1_out = Selected ? Address : 8'bz;  // Controlled_Buffer controlled_buffer_1
  Pull_Resistor pull_resistor_1 (.node(controlled_buffer_1_out));
  Comparator comparator_1 (.a(controlled_buffer_1_out), .b({8{1'b1}}), .eq(Cell_CSC));  // open: gt, lt
  Comparator comparator_2 (.a(controlled_buffer_1_out), .b(8'hfe), .eq(Cell_CSR));  // open: gt, lt
  Comparator comparator_3 (.a(controlled_buffer_1_out), .b(8'hfd), .eq(Table__CSC__CSR____Task_CS));  // open: gt, lt
  Comparator comparator_4 (.a(controlled_buffer_1_out), .b(8'hfc), .eq(SPI_KBD_control));  // open: gt, lt
  Comparator comparator_5 (.a(controlled_buffer_1_out), .b(8'hfb), .eq(Universal_IO_1));  // open: gt, lt
  Comparator comparator_6 (.a(controlled_buffer_1_out), .b(8'hfa), .eq(Universal_IO_2));  // open: gt, lt
  Comparator comparator_7 (.a(controlled_buffer_1_out), .b(8'hf9), .eq(Debug_output));  // open: gt, lt
  or or_1 (Is_IO, Cell_CSC, Cell_CSR, Table__CSC__CSR____Task_CS, SPI_KBD_control, Universal_IO_1, Universal_IO_2, Debug_output);
endmodule
