// Logisim project cell controller.circ as structural Verilog: 2 circuits, main circuit Cell controller
module Cell_controller (
  input  CSR,
  input  [11:0] in_2,
  input  CSC,
  input  [1:0] SPI,
  input  [11:0] in_5,
  input  [11:0] in_6,
  input  [11:0] in_7,
  output [11:0] out_8,
  output MISO,
  output [11:0] out_10,
  output [11:0] out_11,
  output [11:0] out_12,
  output [4:0] out_13,
  output [4:0] out_14,
  output [4:0] out_15,
  output [4:0] out_16,
  output [4:0] out_17,
  output [4:0] out_18,
  output [4:0] out_19,
  output [4:0] out_20,
  output [4:0] out_21,
  output [4:0] out_22,
  output [4:0] out_23,
  output [7:0] out_24,
  output [7:0] out_25,
  output [7:0] out_26,
  output [7:0] out_27,
  output [7:0] out_28,
  output [7:0] out_29,
  output [7:0] out_30,
  output [7:0] out_31,
  output [7:0] out_32,
  output [7:0] out_33,
  output [7:0] out_34,
  output [7:0] out_35,
  output [7:0] out_36,
  output [7:0] out_37,
  output [7:0] out_38,
  output [7:0] out_39,
  output [7:0] out_40,
  output [7:0] out_41,
  output [7:0] out_42,
  output [7:0] out_43,
  output [7:0] out_44,
  output [7:0] out_45
);

  wire and_1_out, spi_module_cell_1_task_conf;
  wire [1:0] spi_module_cell_1_type_select_out, \task , \здфнук_reg_q ;
  wire [3:0] type_reg_q, undriven;
  wire [10:0] Energy;

  and and_1 (and_1_out, CSR, CSC);
  SPI_module__cell spi_module_cell_1 (
    .CS(and_1_out), .CLK(SPI[0]), .MOSI(SPI[1]), .is_task(\task ), .task_conf(spi_module_cell_1_task_conf),
    .energy_out(Energy), .type_select_out(spi_module_cell_1_type_select_out), .MISO(MISO));  // open: err, energy_in, type_select_in, player_select_in, clk_out, is_selected, move_end_1, move_end_2, command, input_transanction_end, player_select_out, output_transanction_end
  Register #(.width(4)) type_reg (.D(undriven), .Q(type_reg_q));  // open: en, clk, clr
  Register #(.width(2)) \u_здфнук_reg  (.Q(\здфнук_reg_q ));  // open: D, en, clk, clr
  DotMatrix #(.matrixcols(11), .matrixrows(8)) dotmatrix_1 (
    .col0(out_24), .col1(out_25), .col2(out_26), .col3(out_27), .col4(out_28), .col5(out_29), .col6(out_30),
    .col7(out_31), .col8(out_32), .col9(out_33), .col10(out_34));
  \Чья_Тип  \u_чья_тип_1  (
    .in_1(2'b00), .in_2({\task , 2'b00}), .out_14(out_24), .out_15(out_25), .out_16(out_26), .out_17(out_27),
    .out_18(out_28), .out_19(out_29), .out_20(out_30), .out_21(out_31), .out_22(out_32), .out_23(out_33),
    .out_24(out_34), .out_3(out_35), .out_4(out_36), .out_5(out_37), .out_6(out_38), .out_7(out_39),
    .out_8(out_40), .out_9(out_41), .out_10(out_42), .out_11(out_43), .out_12(out_44), .out_13(out_45));
  DotMatrix #(.matrixcols(11), .matrixrows(8)) dotmatrix_2 (
    .col0(out_35), .col1(out_36), .col2(out_37), .col3(out_38), .col4(out_39), .col5(out_40), .col6(out_41),
    .col7(out_42), .col8(out_43), .col9(out_44), .col10(out_45));
  DotMatrix #(.matrixcols(11), .matrixrows(5)) dotmatrix_3 (
    .col0(out_13), .col1(out_14), .col2(out_15), .col3(out_16), .col4(out_17), .col5(out_18), .col6(out_19),
    .col7(out_20), .col8(out_21), .col9(out_22), .col10(out_23));
  // Цифры цифры_1: pin names not known; wires that end beside it: Energy[9:0], out_13, out_14, out_15, out_16, out_17, out_18, out_19, out_20, out_21, out_22, out_23

  // Other names for the same wires on the sheet: E1[4:0] = out_13; E2[4:0] = out_14; E3[4:0] = out_15;
  //   E4[4:0] = out_16; E5[4:0] = out_17; E6[4:0] = out_18; E7[4:0] = out_19; E8[4:0] = out_20; E9[4:0] = out_21;
  //   E10[4:0] = out_22; E11[4:0] = out_23; О1[7:0] = out_24; О2[7:0] = out_25; О3[7:0] = out_26; О4[7:0] = out_27;
  //   О5[7:0] = out_28; О6[7:0] = out_29; О7[7:0] = out_30; О8[7:0] = out_31; О9[7:0] = out_32; О10[7:0] = out_33;
  //   О11[7:0] = out_34; С1[7:0] = out_35; С2[7:0] = out_36; С3[7:0] = out_37; С4[7:0] = out_38; С5[7:0] = out_39;
  //   С6[7:0] = out_40; С7[7:0] = out_41; С8[7:0] = out_42; С9[7:0] = out_43; С10[7:0] = out_44; С11[7:0] = out_45

  // Notes on the sheet:
  //   SPI: pull=down
  //   CSC: pull=down
  //   CSR: pull=down
  //   Number mtx output
  //   Orange mtx output
  //   Blue mtx output
  //   чип селедект
endmodule

module local_test (
  input  [1:0] in_1,
  input  in_2,
  input  in_3
);

  wire cell_controller_1_miso;
  wire [4:0] cell_controller_1_out_13, cell_controller_1_out_14, cell_controller_1_out_15,
       cell_controller_1_out_16, cell_controller_1_out_17, cell_controller_1_out_18,
       cell_controller_1_out_19, cell_controller_1_out_20, cell_controller_1_out_21,
       cell_controller_1_out_22, cell_controller_1_out_23;
  wire [7:0] cell_controller_1_out_24, cell_controller_1_out_25, cell_controller_1_out_26,
       cell_controller_1_out_27, cell_controller_1_out_28, cell_controller_1_out_29,
       cell_controller_1_out_30, cell_controller_1_out_31, cell_controller_1_out_32,
       cell_controller_1_out_33, cell_controller_1_out_34, cell_controller_1_out_35,
       cell_controller_1_out_36, cell_controller_1_out_37, cell_controller_1_out_38,
       cell_controller_1_out_39, cell_controller_1_out_40, cell_controller_1_out_41,
       cell_controller_1_out_42, cell_controller_1_out_43, cell_controller_1_out_44, cell_controller_1_out_45;

  DotMatrix #(.matrixcols(11), .matrixrows(5)) dotmatrix_1 (
    .col0(cell_controller_1_out_13), .col1(cell_controller_1_out_14), .col2(cell_controller_1_out_15),
    .col3(cell_controller_1_out_16), .col4(cell_controller_1_out_17), .col5(cell_controller_1_out_18),
    .col6(cell_controller_1_out_19), .col7(cell_controller_1_out_20), .col8(cell_controller_1_out_21),
    .col9(cell_controller_1_out_22), .col10(cell_controller_1_out_23));
  Cell_controller cell_controller_1 (
    .out_13(cell_controller_1_out_13), .out_24(cell_controller_1_out_24), .out_14(cell_controller_1_out_14),
    .out_35(cell_controller_1_out_35), .out_25(cell_controller_1_out_25), .out_15(cell_controller_1_out_15),
    .out_36(cell_controller_1_out_36), .out_26(cell_controller_1_out_26), .out_16(cell_controller_1_out_16),
    .out_37(cell_controller_1_out_37), .out_17(cell_controller_1_out_17), .out_27(cell_controller_1_out_27),
    .out_38(cell_controller_1_out_38), .out_18(cell_controller_1_out_18), .out_28(cell_controller_1_out_28),
    .out_19(cell_controller_1_out_19), .out_39(cell_controller_1_out_39), .out_29(cell_controller_1_out_29),
    .out_20(cell_controller_1_out_20), .out_40(cell_controller_1_out_40), .out_30(cell_controller_1_out_30),
    .out_21(cell_controller_1_out_21), .out_41(cell_controller_1_out_41), .out_22(cell_controller_1_out_22),
    .out_31(cell_controller_1_out_31), .out_42(cell_controller_1_out_42), .out_23(cell_controller_1_out_23),
    .out_32(cell_controller_1_out_32), .out_43(cell_controller_1_out_43), .out_33(cell_controller_1_out_33),
    .out_44(cell_controller_1_out_44), .out_34(cell_controller_1_out_34), .out_45(cell_controller_1_out_45),
    .CSC(in_2), .CSR(in_3), .MISO(cell_controller_1_miso), .SPI(in_1));  // open: in_5, out_11, in_2, out_8, in_6, out_10, in_7, out_12
  DotMatrix #(.matrixcols(11), .matrixrows(8)) dotmatrix_2 (
    .col0(cell_controller_1_out_24), .col1(cell_controller_1_out_25), .col2(cell_controller_1_out_26),
    .col3(cell_controller_1_out_27), .col4(cell_controller_1_out_28), .col5(cell_controller_1_out_29),
    .col6(cell_controller_1_out_30), .col7(cell_controller_1_out_31), .col8(cell_controller_1_out_32),
    .col9(cell_controller_1_out_33), .col10(cell_controller_1_out_34));
  DotMatrix #(.matrixcols(11), .matrixrows(8)) dotmatrix_3 (
    .col0(cell_controller_1_out_35), .col1(cell_controller_1_out_36), .col2(cell_controller_1_out_37),
    .col3(cell_controller_1_out_38), .col4(cell_controller_1_out_39), .col5(cell_controller_1_out_40),
    .col6(cell_controller_1_out_41), .col7(cell_controller_1_out_42), .col8(cell_controller_1_out_43),
    .col9(cell_controller_1_out_44), .col10(cell_controller_1_out_45));

  // Notes on the sheet:
  //   in_1: pull=down
  //   in_2: pull=down
  //   in_3: pull=down
endmodule
