// Logisim project display controller.circ as structural Verilog: 20 circuits, main circuit Type
module Type (
  input  in_1,
  input  [3:0] in_2,
  output [7:0] out_3,
  output [7:0] out_4,
  output [7:0] out_5,
  output [7:0] out_6,
  output [7:0] out_7,
  output [7:0] out_8,
  output [7:0] out_9,
  output [7:0] out_10,
  output [7:0] out_11,
  output [7:0] out_12,
  output [7:0] out_13
);

  wire and_1_out, and_2_out, decoder_1_out0, decoder_1_out1, decoder_1_out2, decoder_1_out3, decoder_1_out4,
       or_1_out, or_2_out;
  wire [2:2] or_3_out;

  Decoder #(.select(3)) decoder_1 (
    .out0(decoder_1_out0), .out1(decoder_1_out1), .out2(decoder_1_out2), .out3(decoder_1_out3),
    .out4(decoder_1_out4), .sel({or_3_out[2], in_2[1:0]}), .en(or_1_out));  // open: out5, out6, out7
  or or_1 (or_1_out, or_3_out[2], in_1);
  or or_2 (or_2_out, decoder_1_out0, in_2[0], in_2[1], in_2[2], in_2[3]);
  DotMatrix #(.matrixcols(11), .matrixrows(8)) dotmatrix_1 (
    .col0(out_3), .col1(out_4), .col2(out_5), .col3(out_6), .col4(out_7), .col5(out_8), .col6(out_9),
    .col7(out_10), .col8(out_11), .col9(out_12), .col10(out_13));
  Pull_Resistor pull_resistor_1 (.node(decoder_1_out4));
  or or_3 (or_3_out[2], in_2[2], in_2[3]);
  and and_1 (and_1_out, decoder_1_out4, in_2[2]);
  and and_2 (and_2_out, decoder_1_out4, in_2[3]);
  Pull_Resistor pull_resistor_2 (.node(decoder_1_out0));
  Pull_Resistor pull_resistor_3 (.node(decoder_1_out1));
  Pull_Resistor pull_resistor_4 (.node(decoder_1_out3));
  Pull_Resistor pull_resistor_5 (.node(decoder_1_out2));
  Pull_Resistor pull_resistor_6 (.node(and_1_out));
  Pull_Resistor pull_resistor_7 (.node(and_2_out));
  Transistor #(.\type ("n"), .width(8)) transistor_1 (.in({8{1'b1}}), .out(out_3), .gate(decoder_1_out0));
  Transistor #(.\type ("n"), .width(8)) transistor_2 (.in({8{1'b1}}), .out(out_4), .gate(decoder_1_out0));
  Transistor #(.\type ("n"), .width(8)) transistor_3 (.in({8{1'b1}}), .out(out_5), .gate(decoder_1_out0));
  Transistor #(.\type ("n"), .width(8)) transistor_4 (.in({8{1'b1}}), .out(out_6), .gate(decoder_1_out0));
  Transistor #(.\type ("n"), .width(8)) transistor_5 (.in({8{1'b1}}), .out(out_7), .gate(decoder_1_out0));
  Transistor #(.\type ("n"), .width(8)) transistor_6 (.in({8{1'b1}}), .out(out_10), .gate(decoder_1_out0));
  Transistor #(.\type ("n"), .width(8)) transistor_7 (.in({8{1'b1}}), .out(out_9), .gate(decoder_1_out0));
  Transistor #(.\type ("n"), .width(8)) transistor_8 (.in({8{1'b1}}), .out(out_11), .gate(decoder_1_out0));
  Transistor #(.\type ("n"), .width(8)) transistor_9 (.in({8{1'b1}}), .out(out_8), .gate(decoder_1_out0));
  Transistor #(.\type ("n"), .width(8)) transistor_10 (.in({8{1'b1}}), .out(out_12), .gate(decoder_1_out0));
  Transistor #(.\type ("n"), .width(8)) transistor_11 (.in({8{1'b1}}), .out(out_13), .gate(decoder_1_out0));
  Transistor #(.\type ("n"), .width(8)) transistor_12 (.in(8'he7), .out(out_3), .gate(decoder_1_out1));
  Transistor #(.\type ("n"), .width(8)) transistor_13 (.in(8'he7), .out(out_6), .gate(decoder_1_out1));
  Transistor #(.\type ("n"), .width(8)) transistor_14 (.in(8'he7), .out(out_5), .gate(decoder_1_out1));
  Transistor #(.\type ("n"), .width(8)) transistor_15 (.in({8{1'b0}}), .out(out_7), .gate(decoder_1_out1));
  Transistor #(.\type ("n"), .width(8)) transistor_16 (.in(8'he7), .out(out_4), .gate(decoder_1_out1));
  Transistor #(.\type ("n"), .width(8)) transistor_17 (.in({8{1'b0}}), .out(out_8), .gate(decoder_1_out1));
  Transistor #(.\type ("n"), .width(8)) transistor_18 (.in(8'he7), .out(out_11), .gate(decoder_1_out1));
  Transistor #(.\type ("n"), .width(8)) transistor_19 (.in(8'he7), .out(out_10), .gate(decoder_1_out1));
  Transistor #(.\type ("n"), .width(8)) transistor_20 (.in({8{1'b0}}), .out(out_9), .gate(decoder_1_out1));
  Transistor #(.\type ("n"), .width(8)) transistor_21 (.in(8'he7), .out(out_13), .gate(decoder_1_out1));
  Transistor #(.\type ("n"), .width(8)) transistor_22 (.in(8'he7), .out(out_12), .gate(decoder_1_out1));
  Transistor #(.\type ("n"), .width(8)) transistor_23 (.in({8{1'b0}}), .out(out_4), .gate(decoder_1_out2));
  Transistor #(.\type ("n"), .width(8)) transistor_24 (.in(8'h6c), .out(out_6), .gate(decoder_1_out2));
  Transistor #(.\type ("n"), .width(8)) transistor_25 (.in({8{1'b1}}), .out(out_3), .gate(decoder_1_out2));
  Transistor #(.\type ("n"), .width(8)) transistor_26 (.in(8'hf8), .out(out_5), .gate(decoder_1_out2));
  Transistor #(.\type ("n"), .width(8)) transistor_27 (.in(8'hd3), .out(out_8), .gate(decoder_1_out2));
  Transistor #(.\type ("n"), .width(8)) transistor_28 (.in(8'h6c), .out(out_10), .gate(decoder_1_out2));
  Transistor #(.\type ("n"), .width(8)) transistor_29 (.in(8'h56), .out(out_7), .gate(decoder_1_out2));
  Transistor #(.\type ("n"), .width(8)) transistor_30 (.in(8'h56), .out(out_9), .gate(decoder_1_out2));
  Transistor #(.\type ("n"), .width(8)) transistor_31 (.in({8{1'b1}}), .out(out_13), .gate(decoder_1_out2));
  Transistor #(.\type ("n"), .width(8)) transistor_32 (.in(8'hf8), .out(out_11), .gate(decoder_1_out2));
  Transistor #(.\type ("n"), .width(8)) transistor_33 (.in({8{1'b0}}), .out(out_12), .gate(decoder_1_out2));
  Transistor #(.\type ("n"), .width(8)) transistor_34 (.in(8'h91), .out(out_3), .gate(decoder_1_out3));
  Transistor #(.\type ("n"), .width(8)) transistor_35 (.in(8'h4a), .out(out_5), .gate(decoder_1_out3));
  Transistor #(.\type ("n"), .width(8)) transistor_36 (.in({8{1'b0}}), .out(out_4), .gate(decoder_1_out3));
  Transistor #(.\type ("n"), .width(8)) transistor_37 (.in(8'h39), .out(out_7), .gate(decoder_1_out3));
  Transistor #(.\type ("n"), .width(8)) transistor_38 (.in(8'h18), .out(out_6), .gate(decoder_1_out3));
  Transistor #(.\type ("n"), .width(8)) transistor_39 (.in(8'h6b), .out(out_8), .gate(decoder_1_out3));
  Transistor #(.\type ("n"), .width(8)) transistor_40 (.in(8'hce), .out(out_9), .gate(decoder_1_out3));
  Transistor #(.\type ("n"), .width(8)) transistor_41 (.in(8'h29), .out(out_11), .gate(decoder_1_out3));
  Transistor #(.\type ("n"), .width(8)) transistor_42 (.in(8'h80), .out(out_12), .gate(decoder_1_out3));
  Transistor #(.\type ("n"), .width(8)) transistor_43 (.in(8'h12), .out(out_13), .gate(decoder_1_out3));
  Transistor #(.\type ("n"), .width(8)) transistor_44 (.in(8'hc), .out(out_10), .gate(decoder_1_out3));
  Transistor #(.\type ("n"), .width(8)) transistor_45 (.in(8'hc0), .out(out_5), .gate(and_1_out));
  Transistor #(.\type ("n"), .width(8)) transistor_46 (.in(8'hc0), .out(out_3), .gate(and_1_out));
  Transistor #(.\type ("n"), .width(8)) transistor_47 (.in(8'hc0), .out(out_4), .gate(and_1_out));
  Transistor #(.\type ("n"), .width(8)) transistor_48 (.in(8'hc0), .out(out_8), .gate(and_1_out));
  Transistor #(.\type ("n"), .width(8)) transistor_49 (.in(8'hc0), .out(out_7), .gate(and_1_out));
  Transistor #(.\type ("n"), .width(8)) transistor_50 (.in(8'hc0), .out(out_6), .gate(and_1_out));
  Transistor #(.\type ("n"), .width(8)) transistor_51 (.in(8'hc0), .out(out_9), .gate(and_1_out));
  Transistor #(.\type ("n"), .width(8)) transistor_52 (.in(8'hc0), .out(out_10), .gate(and_1_out));
  Transistor #(.\type ("n"), .width(8)) transistor_53 (.in(8'hc0), .out(out_13), .gate(and_1_out));
  Transistor #(.\type ("n"), .width(8)) transistor_54 (.in(8'hc0), .out(out_11), .gate(and_1_out));
  Transistor #(.\type ("n"), .width(8)) transistor_55 (.in(8'hc0), .out(out_12), .gate(and_1_out));
  Transistor #(.\type ("n"), .width(8)) transistor_56 (.in(8'h3), .out(out_4), .gate(and_2_out));
  Transistor #(.\type ("n"), .width(8)) transistor_57 (.in(8'h3), .out(out_3), .gate(and_2_out));
  Transistor #(.\type ("n"), .width(8)) transistor_58 (.in(8'h3), .out(out_8), .gate(and_2_out));
  Transistor #(.\type ("n"), .width(8)) transistor_59 (.in(8'h3), .out(out_5), .gate(and_2_out));
  Transistor #(.\type ("n"), .width(8)) transistor_60 (.in(8'h3), .out(out_6), .gate(and_2_out));
  Transistor #(.\type ("n"), .width(8)) transistor_61 (.in(8'h3), .out(out_7), .gate(and_2_out));
  Transistor #(.\type ("n"), .width(8)) transistor_62 (.in(8'h3), .out(out_9), .gate(and_2_out));
  Transistor #(.\type ("n"), .width(8)) transistor_63 (.in(8'h3), .out(out_11), .gate(and_2_out));
  Transistor #(.\type ("n"), .width(8)) transistor_64 (.in(8'h3), .out(out_12), .gate(and_2_out));
  Transistor #(.\type ("n"), .width(8)) transistor_65 (.in(8'h3), .out(out_10), .gate(and_2_out));
  Transistor #(.\type ("n"), .width(8)) transistor_66 (.in(8'h3), .out(out_13), .gate(and_2_out));
  Transistor #(.width(8)) transistor_67 (.in({8{1'b0}}), .out(out_3), .gate(or_2_out));
  Transistor #(.width(8)) transistor_68 (.in({8{1'b0}}), .out(out_4), .gate(or_2_out));
  Transistor #(.width(8)) transistor_69 (.in({8{1'b0}}), .out(out_7), .gate(or_2_out));
  Transistor #(.width(8)) transistor_70 (.in({8{1'b0}}), .out(out_6), .gate(or_2_out));
  Transistor #(.width(8)) transistor_71 (.in({8{1'b0}}), .out(out_5), .gate(or_2_out));
  Transistor #(.width(8)) transistor_72 (.in({8{1'b0}}), .out(out_9), .gate(or_2_out));
  Transistor #(.width(8)) transistor_73 (.in({8{1'b0}}), .out(out_10), .gate(or_2_out));
  Transistor #(.width(8)) transistor_74 (.in({8{1'b0}}), .out(out_8), .gate(or_2_out));
  Transistor #(.width(8)) transistor_75 (.in({8{1'b0}}), .out(out_11), .gate(or_2_out));
  Transistor #(.width(8)) transistor_76 (.in({8{1'b0}}), .out(out_12), .gate(or_2_out));
  Transistor #(.width(8)) transistor_77 (.in({8{1'b0}}), .out(out_13), .gate(or_2_out));

  // Notes on the sheet:
  //   Транспорт
  //   2
  //   Щит
  //   3
  //   4
  //   Энергия
  //   Занята
  //   1
  //   Занята
  //   1
  //   Занята
  //   1
  //   Занята
  //   1
endmodule

module Player_Type (
  input  [1:0] in_1,
  input  [3:0] in_2,
  output [7:0] out_3,
  output [7:0] out_4,
  output [7:0] out_5,
  output [7:0] out_6,
  output [7:0] out_7,
  output [7:0] out_8,
  output [7:0] out_9,
  output [7:0] out_10,
  output [7:0] out_11,
  output [7:0] out_12,
  output [7:0] out_13,
  output [7:0] out_14,
  output [7:0] out_15,
  output [7:0] out_16,
  output [7:0] out_17,
  output [7:0] out_18,
  output [7:0] out_19,
  output [7:0] out_20,
  output [7:0] out_21,
  output [7:0] out_22,
  output [7:0] out_23,
  output [7:0] out_24
);

  wire and_5_out, and_6_out;
  wire [2:0] and_1_out;
  wire [3:0] and_3_out;

  and and_1 (and_1_out[0], in_1[0], in_2[0]);
  and and_2 (and_1_out[1], in_2[1], in_1[0]);
  and and_3 (and_3_out[0], in_1[1], in_2[0]);
  and and_4 (and_3_out[1], in_1[1], in_2[1]);
  xor xor_1 (and_3_out[3], in_2[3], and_6_out);
  xor xor_2 (and_1_out[2], in_2[2], and_5_out);
  and and_5 (and_5_out, in_1[0], in_2[2]);
  and and_6 (and_6_out, in_1[1], in_2[3]);
  DotMatrix #(.matrixcols(11), .matrixrows(8)) dotmatrix_1 (
    .col0(out_14), .col1(out_15), .col2(out_16), .col3(out_17), .col4(out_18), .col5(out_19), .col6(out_20),
    .col7(out_21), .col8(out_22), .col9(out_23), .col10(out_24));
  Type type_1 (
    .in_1(in_1[0]), .in_2({1'b0, and_1_out}), .out_3(out_14), .out_4(out_15), .out_5(out_16), .out_6(out_17),
    .out_7(out_18), .out_8(out_19), .out_9(out_20), .out_10(out_21), .out_11(out_22), .out_12(out_23),
    .out_13(out_24));
  DotMatrix #(.matrixcols(11), .matrixrows(8)) dotmatrix_2 (
    .col0(out_3), .col1(out_4), .col2(out_5), .col3(out_6), .col4(out_7), .col5(out_8), .col6(out_9),
    .col7(out_10), .col8(out_11), .col9(out_12), .col10(out_13));
  Type type_2 (
    .in_1(in_1[1]), .in_2({and_3_out[3], 1'b0, and_3_out[1:0]}), .out_3(out_3), .out_4(out_4), .out_5(out_5),
    .out_6(out_6), .out_7(out_7), .out_8(out_8), .out_9(out_9), .out_10(out_10), .out_11(out_11),
    .out_12(out_12), .out_13(out_13));

  // Notes on the sheet:
  //   Оранжевый
  //   Синий
endmodule

module Col_1 (
  input  D,
  input  C,
  input  B,
  input  A,
  output e,
  output d_2,
  output c_2,
  output b_2,
  output a_2
);

  wire and_1_out, and_2_out, and_3_out, and_4_out, and_5_out, and_6_out, and_7_out, and_8_out, and_9_out,
       and_10_out, and_11_out, and_12_out, and_13_out, and_14_out, and_15_out, and_16_out, and_17_out,
       and_18_out;

  and and_1 (and_1_out, ~D, ~C);  // AND_Gate
  and and_2 (and_2_out, ~C, ~B);  // AND_Gate
  and and_3 (and_3_out, ~D, ~B, A);  // AND_Gate
  and and_4 (and_4_out, ~D, B, ~A);  // AND_Gate
  and and_5 (and_5_out, ~D, ~C, ~A);  // AND_Gate
  and and_6 (and_6_out, ~C, ~B, ~A);  // AND_Gate
  and and_7 (and_7_out, ~D, B, ~A);  // AND_Gate
  and and_8 (and_8_out, ~D, ~A);  // AND_Gate
  and and_9 (and_9_out, ~D, ~C, B);  // AND_Gate
  and and_10 (and_10_out, ~D, C, ~B);  // AND_Gate
  and and_11 (and_11_out, D, ~C, ~B);  // AND_Gate
  and and_12 (and_12_out, ~D, ~B);  // AND_Gate
  and and_13 (and_13_out, ~C, ~B);  // AND_Gate
  and and_14 (and_14_out, ~D, C, ~A);  // AND_Gate
  and and_15 (and_15_out, ~D, ~A);  // AND_Gate
  and and_16 (and_16_out, ~D, B);  // AND_Gate
  and and_17 (and_17_out, ~D, C);  // AND_Gate
  and and_18 (and_18_out, D, ~C, ~B);  // AND_Gate
  or or_1 (e, and_1_out, and_2_out, and_3_out, and_4_out);
  or or_2 (d_2, and_5_out, and_6_out, and_7_out);
  or or_3 (c_2, and_8_out, and_9_out, and_10_out, and_11_out);
  or or_4 (b_2, and_12_out, and_13_out, and_14_out);
  or or_5 (a_2, and_15_out, and_16_out, and_17_out, and_18_out);
endmodule

module Col_2 (
  input  D,
  input  C,
  input  B,
  input  A,
  output e,
  output d_2,
  output c_2,
  output b_2,
  output a_2
);

  wire and_1_out, and_2_out, and_3_out, and_4_out, and_5_out, and_6_out, and_7_out, and_8_out, and_9_out,
       and_10_out, and_11_out, and_12_out;

  and and_1 (and_1_out, ~D, ~C);  // AND_Gate
  and and_2 (and_2_out, ~C, ~B);  // AND_Gate
  and and_3 (and_3_out, ~D, ~B, A);  // AND_Gate
  and and_4 (and_4_out, ~D, B, ~A);  // AND_Gate
  and and_5 (and_5_out, ~D, ~C, A);  // AND_Gate
  and and_6 (and_6_out, ~D, ~C, B);  // AND_Gate
  and and_7 (and_7_out, ~D, C, ~B);  // AND_Gate
  and and_8 (and_8_out, ~D, C, ~A);  // AND_Gate
  and and_9 (and_9_out, D, ~C, ~B);  // AND_Gate
  and and_10 (and_10_out, ~C, ~B);  // AND_Gate
  and and_11 (and_11_out, ~D, A);  // AND_Gate
  and and_12 (and_12_out, ~D, B);  // AND_Gate
  or or_1 (e, and_1_out, and_2_out, and_3_out, and_4_out);
  and and_13 (d_2, ~D, ~C, ~B, A);  // AND_Gate
  or or_2 (c_2, and_5_out, and_6_out, and_7_out, and_8_out, and_9_out);
  and and_14 (b_2, ~D, ~C, ~B, A);  // AND_Gate
  or or_3 (a_2, and_10_out, and_11_out, and_12_out);
endmodule

module Col_3 (
  input  D,
  input  C,
  input  B,
  input  A,
  output e,
  output d_2,
  output c_2,
  output b_2,
  output a_2
);

  wire and_1_out, and_2_out, and_3_out, and_4_out, and_5_out, and_6_out, and_7_out, and_8_out, and_9_out,
       and_10_out, and_11_out, and_12_out, and_13_out, and_14_out, and_15_out, and_16_out, and_17_out;

  and and_1 (and_1_out, ~C, ~B);  // AND_Gate
  and and_2 (and_2_out, ~D, ~B, ~A);  // AND_Gate
  and and_3 (and_3_out, ~D, B, A);  // AND_Gate
  and and_4 (and_4_out, ~D, C);  // AND_Gate
  and and_5 (and_5_out, D, ~C, ~B);  // AND_Gate
  and and_6 (and_6_out, ~D, ~A);  // AND_Gate
  and and_7 (and_7_out, ~D, B);  // AND_Gate
  and and_8 (and_8_out, ~D, C);  // AND_Gate
  and and_9 (and_9_out, D, ~C, ~B);  // AND_Gate
  and and_10 (and_10_out, ~D, ~C, ~A);  // AND_Gate
  and and_11 (and_11_out, ~D, ~B, ~A);  // AND_Gate
  and and_12 (and_12_out, ~D, B, A);  // AND_Gate
  and and_13 (and_13_out, D, ~C, ~B);  // AND_Gate
  and and_14 (and_14_out, ~D, ~A);  // AND_Gate
  and and_15 (and_15_out, ~D, B);  // AND_Gate
  and and_16 (and_16_out, ~D, C);  // AND_Gate
  and and_17 (and_17_out, D, ~C, ~B);  // AND_Gate
  or or_1 (e, ~D, and_1_out);  // OR_Gate
  or or_2 (d_2, and_2_out, and_3_out, and_4_out, and_5_out);
  or or_3 (c_2, and_6_out, and_7_out, and_8_out, and_9_out);
  or or_4 (b_2, and_10_out, and_11_out, and_12_out, and_13_out);
  or or_5 (a_2, and_14_out, and_15_out, and_16_out, and_17_out);
endmodule

module Big_col_1 (
  input  Inversion,
  input  Zero,
  input  D,
  input  C,
  input  B,
  input  A,
  output [14:0] out_7
);

  wire and_1_out, and_2_out, and_3_out, and_4_out, and_5_out, and_6_out, and_7_out, and_8_out, and_9_out,
       and_10_out, and_11_out, and_12_out, and_13_out, and_14_out, and_15_out, and_16_out, and_17_out,
       and_18_out, and_19_out, or_1_out, or_2_out, or_3_out, or_4_out, or_5_out, or_6_out;
  wire [14:0] not_1_out;
  wire [14:2] and_20_out;

  and and_1 (and_1_out, ~D, ~C);  // AND_Gate
  and and_2 (and_2_out, ~C, ~B);  // AND_Gate
  and and_3 (and_3_out, ~D, ~B, A);  // AND_Gate
  and and_4 (and_4_out, ~D, B, ~A);  // AND_Gate
  and and_5 (and_5_out, ~D, ~C, ~A);  // AND_Gate
  and and_6 (and_6_out, ~C, ~B, ~A);  // AND_Gate
  and and_7 (and_7_out, ~D, B, ~A);  // AND_Gate
  and and_8 (and_8_out, A, C, ~B, D);  // AND_Gate
  or or_1 (or_1_out, and_1_out, and_2_out, and_3_out, and_4_out);
  or or_2 (or_2_out, and_5_out, and_6_out, and_7_out);
  and and_9 (and_9_out, ~D, ~A);  // AND_Gate
  and and_10 (and_10_out, ~D, ~C, B);  // AND_Gate
  and and_11 (and_11_out, ~D, C, ~B);  // AND_Gate
  and and_12 (and_12_out, D, ~C, ~B);  // AND_Gate
  and and_13 (and_13_out, ~D, ~B);  // AND_Gate
  or or_3 (or_3_out, and_13_out, and_14_out, and_15_out);
  and and_14 (and_14_out, ~C, ~B);  // AND_Gate
  and and_15 (and_15_out, ~D, C, ~A);  // AND_Gate
  and and_16 (and_16_out, ~D, ~A);  // AND_Gate
  and and_17 (and_17_out, ~D, B);  // AND_Gate
  and and_18 (and_18_out, ~D, C);  // AND_Gate
  and and_19 (and_19_out, D, ~C, ~B);  // AND_Gate
  or or_4 (or_4_out, and_9_out, and_10_out, and_11_out, and_12_out);
  or or_5 (or_5_out, and_16_out, and_17_out, and_18_out, and_19_out);
  and and_20 (and_20_out[2], Zero, or_1_out);
  and and_21 (and_20_out[5], Zero, or_2_out);
  and and_22 (and_20_out[11], Zero, or_3_out);
  and and_23 (and_20_out[14], Zero, or_5_out);
  and and_24 (and_20_out[8], Zero, or_6_out);
  or or_6 (or_6_out, or_4_out, and_8_out);
  Multiplexer #(.width(15), .enable("false")) multiplexer_1 (
    .in0({{3{and_20_out[14]}}, {3{and_20_out[11]}}, {3{and_20_out[8]}}, {3{and_20_out[5]}}, {3{and_20_out[2]}}}),
    .in1(not_1_out), .out(out_7), .sel(Inversion));
  assign not_1_out = ~{{3{and_20_out[14]}}, {3{and_20_out[11]}}, {3{and_20_out[8]}}, {3{and_20_out[5]}}, {3{and_20_out[2]}}};  // NOT_Gate not_1, 15 bits wide
endmodule

module Big_col_2 (
  input  Inversion,
  input  Zero,
  input  D,
  input  C,
  input  B,
  input  A,
  output [14:0] out_7
);

  wire and_1_out, and_2_out, and_3_out, and_4_out, and_5_out, and_6_out, and_7_out, and_8_out, and_9_out,
       and_10_out, and_11_out, and_12_out, and_13_out, and_14_out, and_15_out, or_1_out, or_2_out, or_3_out,
       or_4_out;
  wire [14:0] not_1_out;
  wire [14:2] and_16_out;

  and and_1 (and_1_out, ~D, ~C);  // AND_Gate
  and and_2 (and_2_out, ~C, ~B);  // AND_Gate
  and and_3 (and_3_out, ~D, ~B, A);  // AND_Gate
  and and_4 (and_4_out, ~D, B, ~A);  // AND_Gate
  and and_5 (and_5_out, ~D, ~C, ~B, A);  // AND_Gate
  and and_6 (and_6_out, ~D, ~C, A);  // AND_Gate
  and and_7 (and_7_out, ~D, ~C, B);  // AND_Gate
  and and_8 (and_8_out, ~D, C, ~B);  // AND_Gate
  and and_9 (and_9_out, D, C, A);
  and and_10 (and_10_out, D, ~C, ~B);  // AND_Gate
  and and_11 (and_11_out, ~D, ~C, ~B, A);  // AND_Gate
  and and_12 (and_12_out, ~C, ~B);  // AND_Gate
  and and_13 (and_13_out, ~D, A);  // AND_Gate
  and and_14 (and_14_out, ~D, B);  // AND_Gate
  and and_15 (and_15_out, A, C, ~B, D);  // AND_Gate
  or or_1 (or_1_out, and_1_out, and_2_out, and_3_out, and_4_out);
  or or_2 (or_2_out, and_6_out, and_7_out, and_8_out, and_9_out, and_10_out);
  or or_3 (or_3_out, and_12_out, and_13_out, and_14_out);
  and and_16 (and_16_out[2], Zero, or_1_out);
  and and_17 (and_16_out[5], and_5_out, Zero);
  or or_4 (or_4_out, or_2_out, and_15_out);
  and and_18 (and_16_out[8], Zero, or_4_out);
  and and_19 (and_16_out[11], and_11_out, Zero);
  and and_20 (and_16_out[14], or_3_out, Zero);
  assign not_1_out = ~{{3{and_16_out[14]}}, {3{and_16_out[11]}}, {3{and_16_out[8]}}, {3{and_16_out[5]}}, {3{and_16_out[2]}}};  // NOT_Gate not_1, 15 bits wide
  Multiplexer #(.width(15), .enable("false")) multiplexer_1 (
    .in0({{3{and_16_out[14]}}, {3{and_16_out[11]}}, {3{and_16_out[8]}}, {3{and_16_out[5]}}, {3{and_16_out[2]}}}),
    .in1(not_1_out), .out(out_7), .sel(Inversion));
endmodule

module Big_col_3 (
  input  Inversion,
  input  Zero,
  input  D,
  input  C,
  input  B,
  input  A,
  output [14:0] out_7
);

  wire and_1_out, and_2_out, and_3_out, and_4_out, and_5_out, and_6_out, and_7_out, and_8_out, and_9_out,
       and_10_out, and_11_out, and_12_out, and_13_out, and_14_out, and_15_out, and_16_out, and_17_out,
       and_18_out, or_1_out, or_2_out, or_3_out, or_4_out, or_5_out, or_6_out;
  wire [14:0] not_1_out;
  wire [14:2] and_19_out;

  and and_1 (and_1_out, ~C, ~B);  // AND_Gate
  and and_2 (and_2_out, ~D, ~B, ~A);  // AND_Gate
  and and_3 (and_3_out, ~D, B, A);  // AND_Gate
  and and_4 (and_4_out, ~D, C);  // AND_Gate
  and and_5 (and_5_out, D, ~C, ~B);  // AND_Gate
  and and_6 (and_6_out, ~D, ~A);  // AND_Gate
  and and_7 (and_7_out, ~D, B);  // AND_Gate
  and and_8 (and_8_out, ~D, C);  // AND_Gate
  and and_9 (and_9_out, D, ~C, ~B);  // AND_Gate
  and and_10 (and_10_out, ~D, ~C, ~A);  // AND_Gate
  and and_11 (and_11_out, ~D, ~B, ~A);  // AND_Gate
  and and_12 (and_12_out, ~D, B, A);  // AND_Gate
  and and_13 (and_13_out, D, ~C, ~B);  // AND_Gate
  and and_14 (and_14_out, ~D, ~A);  // AND_Gate
  and and_15 (and_15_out, ~D, B);  // AND_Gate
  and and_16 (and_16_out, ~D, C);  // AND_Gate
  and and_17 (and_17_out, D, ~C, ~B);  // AND_Gate
  and and_18 (and_18_out, A, C, ~B, D);  // AND_Gate
  or or_1 (or_1_out, ~D, and_1_out);  // OR_Gate
  or or_2 (or_2_out, and_2_out, and_3_out, and_4_out, and_5_out);
  or or_3 (or_3_out, and_6_out, and_7_out, and_8_out, and_9_out);
  or or_4 (or_4_out, and_10_out, and_11_out, and_12_out, and_13_out);
  or or_5 (or_5_out, and_14_out, and_15_out, and_16_out, and_17_out);
  and and_19 (and_19_out[2], Zero, or_1_out);
  and and_20 (and_19_out[5], Zero, or_2_out);
  or or_6 (or_6_out, or_3_out, and_18_out);
  and and_21 (and_19_out[8], Zero, or_6_out);
  and and_22 (and_19_out[11], Zero, or_4_out);
  and and_23 (and_19_out[14], or_5_out, Zero);
  Multiplexer #(.width(15), .enable("false")) multiplexer_1 (
    .in0({{3{and_19_out[14]}}, {3{and_19_out[11]}}, {3{and_19_out[8]}}, {3{and_19_out[5]}}, {3{and_19_out[2]}}}),
    .in1(not_1_out), .out(out_7), .sel(Inversion));
  assign not_1_out = ~{{3{and_19_out[14]}}, {3{and_19_out[11]}}, {3{and_19_out[8]}}, {3{and_19_out[5]}}, {3{and_19_out[2]}}};  // NOT_Gate not_1, 15 bits wide
endmodule

module Output_big_numder (
  input  [6:0] in_1,
  input  INV,
  output [14:0] out_3,
  output [14:0] out_4,
  output [14:0] out_5,
  output [14:0] out_6,
  output [14:0] out_7,
  output [14:0] out_8,
  output [14:0] out_9,
  output [14:0] out_10,
  output [14:0] out_11
);

  Big_col_1 big_col_1_1 (
    .Zero(in_1[5]), .D(in_1[3]), .C(in_1[2]), .B(in_1[1]), .A(in_1[0]), .out_7(out_3), .Inversion(INV));
  Big_col_2 big_col_2_1 (
    .Zero(in_1[5]), .D(in_1[3]), .C(in_1[2]), .B(in_1[1]), .A(in_1[0]), .out_7(out_6), .Inversion(INV));
  Big_col_3 big_col_3_1 (
    .Zero(in_1[5]), .D(in_1[3]), .C(in_1[2]), .B(in_1[1]), .A(in_1[0]), .out_7(out_9), .Inversion(INV));

  assign out_4 = out_3;
  assign out_5 = out_3;
  assign out_7 = out_6;
  assign out_8 = out_6;
  assign out_10 = out_9;
  assign out_11 = out_9;
endmodule

module Width (
  input  \Принята_ли_клетка ,
  input  new_task,
  output [1:0] out_3,
  output [14:0] out_4,
  output [14:0] out_5,
  output [14:0] out_6,
  output [14:0] out_7,
  output [14:0] out_8,
  output [14:0] out_9,
  output [14:0] out_10,
  output [14:0] out_11,
  output [14:0] out_12
);

  wire [1:0] random_1_out;
  wire [2:0] inc_1_out_2;

  Random #(.width(2), .seed(1)) random_1 (.clk(new_task), .out(random_1_out));  // open: next, clr
  assign out_3 = \Принята_ли_клетка  ? random_1_out : 2'bz;  // Controlled_Buffer controlled_buffer_1
  inc inc_1 (.in_1(random_1_out), .out_2(inc_1_out_2));
  DotMatrix #(.matrixcols(9), .matrixrows(15)) dotmatrix_1 (
    .col0(out_4), .col1(out_4), .col2(out_4), .col3(out_7), .col4(out_7), .col5(out_7), .col6(out_10),
    .col7(out_10), .col8(out_10));
  // Probe on inc_1_out_2
  Big_col_1 big_col_1_1 (
    .Zero(new_task), .D(1'b0), .C(inc_1_out_2[2]), .B(inc_1_out_2[1]), .A(inc_1_out_2[0]), .out_7(out_4),
    .Inversion(1'b0));
  Big_col_2 big_col_2_1 (
    .Zero(new_task), .D(1'b0), .C(inc_1_out_2[2]), .B(inc_1_out_2[1]), .A(inc_1_out_2[0]), .out_7(out_7),
    .Inversion(1'b0));
  Big_col_3 big_col_3_1 (
    .Zero(new_task), .D(1'b0), .C(inc_1_out_2[2]), .B(inc_1_out_2[1]), .A(inc_1_out_2[0]), .out_7(out_10),
    .Inversion(1'b0));

  assign out_5 = out_4;
  assign out_6 = out_4;
  assign out_8 = out_7;
  assign out_9 = out_7;
  assign out_11 = out_10;
  assign out_12 = out_10;
endmodule

module task2_0 (
  input  [15:0] \Удали_меня_позже ,
  input  Clk,
  input  MOSI,
  input  \Фаза_игры 
);

  wire [14:0] height_1_out_4, height_1_out_5, height_1_out_6, height_1_out_7, height_1_out_8, height_1_out_9,
       height_1_out_10, height_1_out_11, height_1_out_12, width_1_out_4, width_1_out_5, width_1_out_6,
       width_1_out_7, width_1_out_8, width_1_out_9, width_1_out_10, width_1_out_11, width_1_out_12;

  input_shifter input_shifter_1 (.MOSI(MOSI), .CLK(Clk));  // open: Reset, Data_out, buffer_ptr
  Width width_1 (
    .new_task(\Фаза_игры ), .out_4(width_1_out_4), .out_5(width_1_out_5), .out_6(width_1_out_6),
    .out_7(width_1_out_7), .out_8(width_1_out_8), .out_9(width_1_out_9), .out_10(width_1_out_10),
    .out_11(width_1_out_11), .out_12(width_1_out_12));  // open: out_3, Принята_ли_клетка
  // AND_Gate and_1 has open pins: in0=\Удали_меня_позже [4], in1=\Фаза_игры , out=open
  DotMatrix #(.matrixcols(9), .matrixrows(15)) dotmatrix_1 (
    .col0(width_1_out_4), .col1(width_1_out_5), .col2(width_1_out_6), .col3(width_1_out_7),
    .col4(width_1_out_8), .col5(width_1_out_9), .col6(width_1_out_10), .col7(width_1_out_11),
    .col8(width_1_out_12));
  height height_1 (
    .new_task(\Фаза_игры ), .out_4(height_1_out_4), .out_5(height_1_out_5), .out_6(height_1_out_6),
    .out_7(height_1_out_7), .out_8(height_1_out_8), .out_9(height_1_out_9), .out_10(height_1_out_10),
    .out_11(height_1_out_11), .out_12(height_1_out_12));  // open: Принята_ли_клетка, out_3
  DotMatrix #(.matrixcols(9), .matrixrows(15)) dotmatrix_2 (
    .col0(height_1_out_4), .col1(height_1_out_5), .col2(height_1_out_6), .col3(height_1_out_7),
    .col4(height_1_out_8), .col5(height_1_out_9), .col6(height_1_out_10), .col7(height_1_out_11),
    .col8(height_1_out_12));
  DotMatrix #(.matrixcols(24), .matrixrows(2)) dotmatrix_3 (
    .col0(2'b11), .col1(2'b11), .col2(2'b11), .col3(2'b11), .col4(2'b11), .col5(2'b11), .col6(2'b11),
    .col7(2'b11), .col8(2'b11), .col9(2'b11), .col10(2'b11), .col11(2'b11), .col12(2'b11), .col13(2'b11),
    .col14(2'b11), .col15(2'b11), .col16(2'b11), .col17(2'b11), .col18(2'b11), .col19(2'b11), .col20(2'b11),
    .col21(2'b11), .col22(2'b11), .col23(2'b11));
  DotMatrix #(.matrixcols(7), .matrixrows(5)) dotmatrix_4 ();  // open: col0, col1, col2, col3, col4, col5, col6
  DotMatrix #(.matrixcols(7), .matrixrows(5)) dotmatrix_5 ();  // open: col0, col1, col2, col3, col4, col5, col6
  DotMatrix #(.matrixcols(24), .matrixrows(2)) dotmatrix_6 (
    .col0(2'b11), .col1(2'b11), .col2(2'b11), .col3(2'b11), .col4(2'b11), .col5(2'b11), .col6(2'b11),
    .col7(2'b11), .col8(2'b11), .col9(2'b11), .col10(2'b11), .col11(2'b11), .col12(2'b11), .col13(2'b11),
    .col14(2'b11), .col15(2'b11), .col16(2'b11), .col17(2'b11), .col18(2'b11), .col19(2'b11), .col20(2'b11),
    .col21(2'b11), .col22(2'b11), .col23(2'b11));
  DotMatrix #(.matrixcols(7), .matrixrows(5)) dotmatrix_7 ();  // open: col0, col1, col2, col3, col4, col5, col6
  DotMatrix #(.matrixcols(7), .matrixrows(5)) dotmatrix_8 ();  // open: col0, col1, col2, col3, col4, col5, col6
  DotMatrix #(.matrixcols(7), .matrixrows(5)) dotmatrix_9 ();  // open: col0, col1, col2, col3, col4, col5, col6
  DotMatrix #(.matrixcols(7), .matrixrows(5)) dotmatrix_10 ();  // open: col0, col1, col2, col3, col4, col5, col6
  DotMatrix #(.matrixcols(23), .matrixrows(2)) dotmatrix_11 (
    .col0(2'b11), .col1(2'b11), .col2(2'b11), .col3(2'b11), .col4(2'b11), .col5(2'b11), .col6(2'b11),
    .col7(2'b11), .col8(2'b11), .col9(2'b11), .col10(2'b11), .col11(2'b11), .col12(2'b11), .col13(2'b11),
    .col14(2'b11), .col15(2'b11), .col16(2'b11), .col17(2'b11), .col18(2'b11), .col19(2'b11), .col20(2'b11),
    .col21(2'b11), .col22(2'b11));
  DotMatrix #(.matrixcols(7), .matrixrows(5)) dotmatrix_12 ();  // open: col0, col1, col2, col3, col4, col5, col6
  DotMatrix #(.matrixcols(7), .matrixrows(5)) dotmatrix_13 ();  // open: col0, col1, col2, col3, col4, col5, col6
  DotMatrix #(.matrixcols(23), .matrixrows(2)) dotmatrix_14 (
    .col0(2'b11), .col1(2'b11), .col2(2'b11), .col3(2'b11), .col4(2'b11), .col5(2'b11), .col6(2'b11),
    .col7(2'b11), .col8(2'b11), .col9(2'b11), .col10(2'b11), .col11(2'b11), .col12(2'b11), .col13(2'b11),
    .col14(2'b11), .col15(2'b11), .col16(2'b11), .col17(2'b11), .col18(2'b11), .col19(2'b11), .col20(2'b11),
    .col21(2'b11), .col22(2'b11));
  DotMatrix #(.matrixcols(7), .matrixrows(5)) dotmatrix_15 ();  // open: col0, col1, col2, col3, col4, col5, col6
  DotMatrix #(.matrixcols(7), .matrixrows(5)) dotmatrix_16 ();  // open: col0, col1, col2, col3, col4, col5, col6
endmodule

module height (
  input  \Принята_ли_клетка ,
  input  new_task,
  output [1:0] out_3,
  output [14:0] out_4,
  output [14:0] out_5,
  output [14:0] out_6,
  output [14:0] out_7,
  output [14:0] out_8,
  output [14:0] out_9,
  output [14:0] out_10,
  output [14:0] out_11,
  output [14:0] out_12
);

  wire [1:0] random_1_out;
  wire [2:0] inc_1_out_2;

  Random #(.width(2)) random_1 (.clk(new_task), .out(random_1_out));  // open: next, clr
  assign out_3 = \Принята_ли_клетка  ? random_1_out : 2'bz;  // Controlled_Buffer controlled_buffer_1
  // Probe on inc_1_out_2
  inc inc_1 (.in_1(random_1_out), .out_2(inc_1_out_2));
  DotMatrix #(.matrixcols(9), .matrixrows(15)) dotmatrix_1 (
    .col0(out_4), .col1(out_4), .col2(out_4), .col3(out_7), .col4(out_7), .col5(out_7), .col6(out_10),
    .col7(out_10), .col8(out_10));
  Big_col_1 big_col_1_1 (
    .Zero(new_task), .D(1'b0), .C(inc_1_out_2[2]), .B(inc_1_out_2[1]), .A(inc_1_out_2[0]), .out_7(out_4),
    .Inversion(1'b0));
  Big_col_2 big_col_2_1 (
    .Zero(new_task), .D(1'b0), .C(inc_1_out_2[2]), .B(inc_1_out_2[1]), .A(inc_1_out_2[0]), .out_7(out_7),
    .Inversion(1'b0));
  Big_col_3 big_col_3_1 (
    .Zero(new_task), .D(1'b0), .C(inc_1_out_2[2]), .B(inc_1_out_2[1]), .A(inc_1_out_2[0]), .out_7(out_10),
    .Inversion(1'b0));

  assign out_5 = out_4;
  assign out_6 = out_4;
  assign out_8 = out_7;
  assign out_9 = out_7;
  assign out_11 = out_10;
  assign out_12 = out_10;
endmodule

module local_test (
  input  [15:0] in_1,
  output [3:0] out_2
);

  wire n, undriven, y;
  wire [14:0] height_1_out_4, height_1_out_5, height_1_out_6, height_1_out_7, height_1_out_8, height_1_out_9,
       height_1_out_10, height_1_out_11, height_1_out_12, width_1_out_4, width_1_out_5, width_1_out_6,
       width_1_out_7, width_1_out_8, width_1_out_9, width_1_out_10, width_1_out_11, width_1_out_12;

  task2_0 task2_0_1 (.\Удали_меня_позже (in_1), .\Фаза_игры (undriven));  // open: Clk, MOSI
  LED led_1 (.in(1'b1));
  LED led_2 (.in(1'b1));
  LED led_3 (.in(1'b1));
  DotMatrix #(.matrixcols(9), .matrixrows(15)) dotmatrix_1 (
    .col0(width_1_out_4), .col1(width_1_out_5), .col2(width_1_out_6), .col3(width_1_out_7),
    .col4(width_1_out_8), .col5(width_1_out_9), .col6(width_1_out_10), .col7(width_1_out_11),
    .col8(width_1_out_12));
  Width width_1 (
    .new_task(undriven), .out_4(width_1_out_4), .out_5(width_1_out_5), .out_6(width_1_out_6),
    .out_7(width_1_out_7), .out_8(width_1_out_8), .out_9(width_1_out_9), .out_10(width_1_out_10),
    .out_11(width_1_out_11), .out_12(width_1_out_12), .out_3(out_2[1:0]), .\Принята_ли_клетка (y));
  LED led_4 (.in(1'b1));
  LED led_5 (.in(1'b1));
  LED led_6 (.in(1'b1));
  LED led_7 (.in(1'b1));
  LED led_8 (.in(1'b1));
  Button button_1 (.out(y));
  LED led_9 (.in(1'b1));
  LED led_10 (.in(1'b1));
  LED led_11 (.in(1'b1));
  LED led_12 (.in(1'b1));
  LED led_13 (.in(1'b1));
  LED led_14 (.in(1'b1));
  Button button_2 (.out(n));
  DotMatrix #(.matrixcols(9), .matrixrows(15)) dotmatrix_2 (
    .col0(height_1_out_4), .col1(height_1_out_5), .col2(height_1_out_6), .col3(height_1_out_7),
    .col4(height_1_out_8), .col5(height_1_out_9), .col6(height_1_out_10), .col7(height_1_out_11),
    .col8(height_1_out_12));
  height height_1 (
    .new_task(undriven), .out_4(height_1_out_4), .out_5(height_1_out_5), .out_6(height_1_out_6),
    .out_7(height_1_out_7), .out_8(height_1_out_8), .out_9(height_1_out_9), .out_10(height_1_out_10),
    .out_11(height_1_out_11), .out_12(height_1_out_12), .\Принята_ли_клетка (y), .out_3(out_2[3:2]));
  // Probe on out_2[1:0]
  // Probe on out_2[3:2]
  // output_shifter output_shifter_1: pin names not known
endmodule

module table_first (
  input  [1:0] Weight,
  input  [1:0] Hight,
  output [4:0] out_3,
  output [4:0] out_4,
  output [4:0] out_5,
  output [4:0] out_6,
  output [4:0] out_7,
  output [4:0] out_8,
  output [4:0] out_9,
  output Busy
);

  wire [2:0] inc_1_out_2, inc_2_out_2;

  inc inc_1 (.in_1(Weight), .out_2(inc_1_out_2));
  inc inc_2 (.in_1(Hight), .out_2(inc_2_out_2));
  Col_1 col_1_1 (
    .D(1'b0), .C(inc_1_out_2[2]), .B(inc_1_out_2[1]), .A(inc_1_out_2[0]), .e(out_3[4]), .d_2(out_3[3]),
    .c_2(out_3[2]), .b_2(out_3[1]), .a_2(out_3[0]));
  Col_2 col_2_1 (
    .D(1'b0), .C(inc_1_out_2[2]), .B(inc_1_out_2[1]), .A(inc_1_out_2[0]), .e(out_4[4]), .d_2(out_4[3]),
    .c_2(out_4[3]), .b_2(out_4[1]), .a_2(out_4[0]));
  Col_3 col_3_1 (
    .D(1'b0), .C(inc_1_out_2[2]), .B(inc_1_out_2[1]), .A(inc_1_out_2[0]), .e(out_5[4]), .d_2(out_5[3]),
    .c_2(out_5[3]), .b_2(out_5[1]), .a_2(out_5[0]));
  Col_1 col_1_2 (
    .D(1'b0), .C(inc_2_out_2[2]), .B(inc_2_out_2[1]), .A(inc_2_out_2[0]), .e(out_7[4]), .d_2(out_7[3]),
    .c_2(out_7[2]), .b_2(out_7[1]), .a_2(out_7[0]));
  Col_2 col_2_2 (
    .D(1'b0), .C(inc_2_out_2[2]), .B(inc_2_out_2[1]), .A(inc_2_out_2[0]), .e(out_8[4]), .d_2(out_8[3]),
    .c_2(out_8[3]), .b_2(out_8[1]), .a_2(out_8[0]));
  Col_3 col_3_2 (
    .D(1'b0), .C(inc_2_out_2[2]), .B(inc_2_out_2[1]), .A(inc_2_out_2[0]), .e(out_9[4]), .d_2(out_9[3]),
    .c_2(out_9[3]), .b_2(out_9[1]), .a_2(out_9[0]));
  or or_1 (Busy, inc_2_out_2[0], inc_2_out_2[1], inc_2_out_2[2]);

  assign out_4[2] = out_4[3];
  assign out_5[2] = out_5[3];
  assign out_6 = {5{1'b0}};
  assign out_8[2] = out_8[3];
  assign out_9[2] = out_9[3];
endmodule

module \table  (
  input  Busy,
  input  [1:0] Weight,
  input  [1:0] Hight,
  output [4:0] out_4,
  output [4:0] out_5,
  output [4:0] out_6,
  output Busy_2,
  output [4:0] out_8,
  output [4:0] out_9,
  output [4:0] out_10,
  output [4:0] out_11
);

  wire [2:0] inc_1_out_2, undriven;
  wire [4:0] col_1_1_a_2, col_2_1_a_2, col_3_1_a_2;

  inc inc_1 (.in_1(Weight), .out_2(inc_1_out_2));
  or or_1 (Busy_2, out_4[0], out_4[1], out_4[2], out_4[3], out_4[4]);
  Multiplexer #(.width(5), .enable("false")) multiplexer_1 (
    .in0({5{1'b0}}), .in1({col_2_1_a_2[4:3], col_2_1_a_2[3], col_2_1_a_2[1:0]}), .out(out_5), .sel(Busy));
  Multiplexer #(.width(5), .enable("false")) multiplexer_2 (
    .in0({5{1'b0}}), .in1(col_1_1_a_2), .out(out_4), .sel(Busy));
  Multiplexer #(.width(5), .enable("false")) multiplexer_3 (
    .in0({5{1'b0}}), .in1({col_3_1_a_2[4:3], col_3_1_a_2[3], col_3_1_a_2[1:0]}), .out(out_6), .sel(Busy));
  Col_1 col_1_1 (
    .D(1'b0), .C(inc_1_out_2[2]), .B(inc_1_out_2[1]), .A(inc_1_out_2[0]), .e(col_1_1_a_2[4]),
    .d_2(col_1_1_a_2[3]), .c_2(col_1_1_a_2[2]), .b_2(col_1_1_a_2[1]), .a_2(col_1_1_a_2[0]));
  Col_2 col_2_1 (
    .D(1'b0), .C(inc_1_out_2[2]), .B(inc_1_out_2[1]), .A(inc_1_out_2[0]), .e(col_2_1_a_2[4]),
    .d_2(col_2_1_a_2[3]), .c_2(col_2_1_a_2[3]), .b_2(col_2_1_a_2[1]), .a_2(col_2_1_a_2[0]));
  Col_3 col_3_1 (
    .D(1'b0), .C(inc_1_out_2[2]), .B(inc_1_out_2[1]), .A(inc_1_out_2[0]), .e(col_3_1_a_2[4]),
    .d_2(col_3_1_a_2[3]), .c_2(col_3_1_a_2[3]), .b_2(col_3_1_a_2[1]), .a_2(col_3_1_a_2[0]));
  Col_1 col_1_2 (
    .D(1'b0), .C(undriven[2]), .B(undriven[1]), .A(undriven[0]), .e(out_9[4]), .d_2(out_9[3]),
    .c_2(out_9[2]), .b_2(out_9[1]), .a_2(out_9[0]));
  Col_2 col_2_2 (
    .D(1'b0), .C(undriven[2]), .B(undriven[1]), .A(undriven[0]), .e(out_10[4]), .d_2(out_10[3]),
    .c_2(out_10[3]), .b_2(out_10[1]), .a_2(out_10[0]));
  Col_3 col_3_2 (
    .D(1'b0), .C(undriven[2]), .B(undriven[1]), .A(undriven[0]), .e(out_11[4]), .d_2(out_11[3]),
    .c_2(out_11[3]), .b_2(out_11[1]), .a_2(out_11[0]));

  assign out_8 = {5{1'b0}};
  assign out_10[2] = out_10[3];
  assign out_11[2] = out_11[3];
endmodule

module Numders (
  input  [9:0] Energy,
  input  in_2,
  output [4:0] out_3,
  output [4:0] out_4,
  output [4:0] out_5,
  output [4:0] out_6,
  output [4:0] out_7,
  output [4:0] out_8,
  output [4:0] out_9,
  output [4:0] out_10,
  output [4:0] out_11,
  output [4:0] out_12,
  output [4:0] out_13
);

  wire and_1_out, or_1_out, or_2_out, or_3_out, or_4_out, or_5_out, or_6_out;
  wire [4:0] not_1_out, not_2_out, not_3_out, not_4_out, not_5_out, not_6_out, not_7_out, not_8_out,
       not_9_out, not_10_out, not_11_out, num_1_out_2, num_1_out_3, num_1_out_4, num_2_out_2, num_2_out_3,
       num_2_out_4, num_3_out_2, num_3_out_3, num_3_out_4, transistor_1_out, transistor_4_out,
       transistor_5_out, transistor_16_out, transistor_17_out, transistor_18_out, transistor_26_out,
       transistor_27_out, transistor_28_out;
  wire [9:0] divider_1_out, divider_1_rem, divider_2_out, divider_2_rem, divider_3_rem, transistor_9_out;

  Num num_1 (.in_1(divider_3_rem), .out_2(num_1_out_2), .out_3(num_1_out_3), .out_4(num_1_out_4));
  Transistor #(.\type ("n"), .width(5)) transistor_1 (.in(num_1_out_2), .out(transistor_1_out), .gate(or_2_out));
  assign not_1_out = ~transistor_1_out;  // NOT_Gate not_1, 5 bits wide
  Transistor #(.width(5)) transistor_2 (.in(transistor_1_out), .out(out_3), .gate(in_2));
  Transistor #(.\type ("n"), .width(5)) transistor_3 (.in(not_1_out), .out(out_3), .gate(in_2));
  Transistor #(.\type ("n"), .width(5)) transistor_4 (.in(num_1_out_3), .out(transistor_4_out), .gate(or_2_out));
  Transistor #(.\type ("n"), .width(5)) transistor_5 (.in(num_1_out_4), .out(transistor_5_out), .gate(or_2_out));
  assign not_2_out = ~transistor_4_out;  // NOT_Gate not_2, 5 bits wide
  Transistor #(.width(5)) transistor_6 (.in(transistor_4_out), .out(out_4), .gate(in_2));
  Transistor #(.width(5)) transistor_7 (.in(transistor_5_out), .out(out_5), .gate(in_2));
  Transistor #(.\type ("n"), .width(5)) transistor_8 (.in(not_2_out), .out(out_4), .gate(in_2));
  Transistor #(.width(10)) transistor_9 (.in(Energy), .out(transistor_9_out), .gate(and_1_out));
  assign not_3_out = ~transistor_5_out;  // NOT_Gate not_3, 5 bits wide
  Transistor #(.\type ("n"), .width(5)) transistor_10 (.in(not_3_out), .out(out_5), .gate(in_2));
  Transistor #(.width(5)) transistor_11 (.in({5{1'b0}}), .out(out_6), .gate(in_2));
  // Probe on Energy
  Transistor #(.\type ("n"), .width(10)) transistor_12 (.in(10'h3e7), .out(transistor_9_out), .gate(and_1_out));
  Divider #(.width(10)) divider_1 (
    .a(transistor_9_out), .b(10'ha), .out(divider_1_out), .rem(divider_1_rem));  // open: upper
  assign not_4_out = ~transistor_16_out;  // NOT_Gate not_4, 5 bits wide
  assign not_5_out = ~{5{1'b0}};  // NOT_Gate not_5, 5 bits wide
  Transistor #(.\type ("n"), .width(5)) transistor_13 (.in(not_5_out), .out(out_6), .gate(in_2));
  Transistor #(.width(5)) transistor_14 (.in(transistor_16_out), .out(out_7), .gate(in_2));
  Transistor #(.\type ("n"), .width(5)) transistor_15 (.in(not_4_out), .out(out_7), .gate(in_2));
  Divider #(.width(10)) divider_2 (
    .a(divider_1_out), .b(10'ha), .out(divider_2_out), .rem(divider_2_rem));  // open: upper
  Num num_2 (.in_1(divider_2_rem), .out_2(num_2_out_2), .out_3(num_2_out_3), .out_4(num_2_out_4));
  Transistor #(.\type ("n"), .width(5)) transistor_16 (.in(num_2_out_2), .out(transistor_16_out), .gate(or_5_out));
  Transistor #(.\type ("n"), .width(5)) transistor_17 (.in(num_2_out_4), .out(transistor_17_out), .gate(or_5_out));
  Transistor #(.\type ("n"), .width(5)) transistor_18 (.in(num_2_out_3), .out(transistor_18_out), .gate(or_5_out));
  assign not_6_out = ~transistor_18_out;  // NOT_Gate not_6, 5 bits wide
  Transistor #(.\type ("n"), .width(5)) transistor_19 (.in(not_6_out), .out(out_8), .gate(in_2));
  Transistor #(.width(5)) transistor_20 (.in(transistor_18_out), .out(out_8), .gate(in_2));
  Divider #(.width(10)) divider_3 (.a(divider_2_out), .b(10'ha), .rem(divider_3_rem));  // open: out, upper
  assign not_7_out = ~transistor_17_out;  // NOT_Gate not_7, 5 bits wide
  Transistor #(.width(5)) transistor_21 (.in({5{1'b0}}), .out(out_10), .gate(in_2));
  Transistor #(.width(5)) transistor_22 (.in(transistor_17_out), .out(out_9), .gate(in_2));
  Transistor #(.\type ("n"), .width(5)) transistor_23 (.in(not_7_out), .out(out_9), .gate(in_2));
  assign not_8_out = ~{5{1'b0}};  // NOT_Gate not_8, 5 bits wide
  Transistor #(.width(5)) transistor_24 (.in(transistor_28_out), .out(out_11), .gate(in_2));
  Transistor #(.\type ("n"), .width(5)) transistor_25 (.in(not_8_out), .out(out_10), .gate(in_2));
  or or_1 (or_1_out, Energy[3], Energy[4]);
  or or_2 (or_2_out, divider_3_rem[0], divider_3_rem[1], divider_3_rem[2], divider_3_rem[3], divider_3_rem[4], divider_3_rem[5], divider_3_rem[6], divider_3_rem[7], divider_3_rem[8], divider_3_rem[9]);
  or or_3 (or_3_out, divider_2_rem[0], divider_2_rem[1], divider_2_rem[2], divider_2_rem[3], divider_2_rem[4], divider_2_rem[5], divider_2_rem[6], divider_2_rem[7], divider_2_rem[8], divider_2_rem[9]);
  or or_4 (or_4_out, divider_1_rem[0], divider_1_rem[1], divider_1_rem[2], divider_1_rem[3], divider_1_rem[4], divider_1_rem[5], divider_1_rem[6], divider_1_rem[7], divider_1_rem[8], divider_1_rem[9]);
  Num num_3 (.in_1(divider_1_rem), .out_2(num_3_out_2), .out_3(num_3_out_3), .out_4(num_3_out_4));
  Transistor #(.\type ("n"), .width(5)) transistor_26 (.in(num_3_out_3), .out(transistor_26_out), .gate(or_6_out));
  Transistor #(.\type ("n"), .width(5)) transistor_27 (.in(num_3_out_4), .out(transistor_27_out), .gate(or_6_out));
  Transistor #(.\type ("n"), .width(5)) transistor_28 (.in(num_3_out_2), .out(transistor_28_out), .gate(or_6_out));
  assign not_9_out = ~transistor_26_out;  // NOT_Gate not_9, 5 bits wide
  assign not_10_out = ~transistor_28_out;  // NOT_Gate not_10, 5 bits wide
  Transistor #(.width(5)) transistor_29 (.in(transistor_26_out), .out(out_12), .gate(in_2));
  Transistor #(.\type ("n"), .width(5)) transistor_30 (.in(not_9_out), .out(out_12), .gate(in_2));
  Transistor #(.\type ("n"), .width(5)) transistor_31 (.in(not_10_out), .out(out_11), .gate(in_2));
  and and_1 (and_1_out, or_1_out, Energy[5], Energy[6], Energy[7], Energy[8], Energy[9]);
  or or_5 (or_5_out, or_3_out, or_2_out);
  or or_6 (or_6_out, or_4_out, or_3_out, or_2_out);
  assign not_11_out = ~transistor_27_out;  // NOT_Gate not_11, 5 bits wide
  Transistor #(.\type ("n"), .width(5)) transistor_32 (.in(not_11_out), .out(out_13), .gate(in_2));
  Transistor #(.width(5)) transistor_33 (.in(transistor_27_out), .out(out_13), .gate(in_2));
  Transistor #(.width(5)) transistor_34 (.in({5{1'b0}}), .out(transistor_1_out), .gate(or_2_out));
  Transistor #(.width(5)) transistor_35 (.in({5{1'b0}}), .out(transistor_4_out), .gate(or_2_out));
  Transistor #(.width(5)) transistor_36 (.in({5{1'b0}}), .out(transistor_18_out), .gate(or_5_out));
  Transistor #(.width(5)) transistor_37 (.in({5{1'b0}}), .out(transistor_16_out), .gate(or_5_out));
  Transistor #(.width(5)) transistor_38 (.in({5{1'b0}}), .out(transistor_26_out), .gate(or_6_out));
  Transistor #(.width(5)) transistor_39 (.in({5{1'b0}}), .out(transistor_28_out), .gate(or_6_out));
  Transistor #(.width(5)) transistor_40 (.in({5{1'b0}}), .out(transistor_5_out), .gate(or_2_out));
  Transistor #(.width(5)) transistor_41 (.in({5{1'b0}}), .out(transistor_17_out), .gate(or_5_out));
  Transistor #(.width(5)) transistor_42 (.in({5{1'b0}}), .out(transistor_27_out), .gate(or_6_out));

  // Notes on the sheet:
  //   еденицы
  //   десятки
  //   сотни
endmodule

module Num (
  input  [9:0] in_1,
  output [4:0] out_2,
  output [4:0] out_3,
  output [4:0] out_4
);

  // Probe on in_1
  Col_1 col_1_1 (
    .D(in_1[3]), .C(in_1[2]), .B(in_1[1]), .A(in_1[0]), .e(out_2[0]), .d_2(out_2[1]), .c_2(out_2[2]),
    .b_2(out_2[3]), .a_2(out_2[4]));
  Col_2 col_2_1 (
    .D(in_1[3]), .C(in_1[2]), .B(in_1[1]), .A(in_1[0]), .e(out_3[0]), .d_2(out_3[1]), .c_2(out_3[2]),
    .b_2(out_3[3]), .a_2(out_3[4]));
  Col_3 col_3_1 (
    .D(in_1[3]), .C(in_1[2]), .B(in_1[1]), .A(in_1[0]), .e(out_4[0]), .d_2(out_4[1]), .c_2(out_4[2]),
    .b_2(out_4[3]), .a_2(out_4[4]));
  DotMatrix #(.matrixcols(3), .matrixrows(5)) dotmatrix_1 (.col0(out_2), .col1(out_3), .col2(out_4));
endmodule

module otladka (
  input  [11:0] in_1,
  input  [11:0] in_2,
  output [4:0] out_3,
  output [4:0] out_4,
  output [4:0] out_5,
  output [4:0] out_6,
  output [4:0] out_7,
  output [4:0] out_8,
  output [4:0] out_9,
  output [4:0] out_10,
  output [4:0] out_11,
  output [4:0] out_12,
  output [4:0] out_13,
  output [4:0] out_14,
  output [4:0] out_15,
  output [4:0] out_16,
  output [4:0] out_17,
  output [4:0] out_18,
  output [4:0] out_19,
  output [4:0] out_20,
  output [4:0] out_21,
  output [11:0] out_22,
  output [11:0] out_23
);

  wire L, or_2_out, R;
  wire [9:0] transistor_4_out;

  Transistor #(.\type ("n"), .width(5)) transistor_1 (.in(5'b00100), .out(out_21), .gate(R));
  Transistor #(.\type ("n"), .width(5)) transistor_2 (.in(5'b01110), .out(out_20), .gate(R));
  or or_1 (L, in_2[0], in_2[1], in_2[2], in_2[3], in_2[4], in_2[5], in_2[6], in_2[7], in_2[8], in_2[9]);
  Transistor #(.\type ("n"), .width(5)) transistor_3 (.in({5{1'b1}}), .out(out_19), .gate(R));
  Transistor #(.\type ("n"), .width(10)) transistor_4 (.in(in_2[9:0]), .out(transistor_4_out), .gate(L));
  Transistor #(.width(5)) transistor_5 (.in({5{1'b0}}), .out(out_21), .gate(R));
  Transistor #(.width(5)) transistor_6 (.in({5{1'b0}}), .out(out_20), .gate(R));
  Transistor #(.width(10)) transistor_7 (.in({10{1'b0}}), .out(transistor_4_out), .gate(or_2_out));
  or or_2 (or_2_out, R, L);
  Transistor #(.width(5)) transistor_8 (.in({5{1'b0}}), .out(out_19), .gate(R));
  Transistor #(.\type ("n"), .width(10)) transistor_9 (.in(in_1[9:0]), .out(transistor_4_out), .gate(R));
  DotMatrix #(.matrixcols(19), .matrixrows(5)) dotmatrix_1 (
    .col0(out_21), .col1(out_20), .col2(out_19), .col3({5{1'b0}}), .col4(out_17), .col5(out_16),
    .col6(out_15), .col7(out_14), .col8(out_13), .col9(out_12), .col10(out_11), .col11(out_10),
    .col12(out_9), .col13(out_8), .col14(out_7), .col15({5{1'b0}}), .col16(out_5), .col17(out_4),
    .col18(out_3));
  Transistor #(.\type ("n"), .width(5)) transistor_10 (.in({5{1'b1}}), .out(out_5), .gate(L));
  Numders numders_1 (
    .Energy(transistor_4_out), .in_2(1'b0), .out_3(out_17), .out_4(out_16), .out_5(out_15), .out_6(out_14),
    .out_7(out_13), .out_8(out_12), .out_9(out_11), .out_10(out_10), .out_11(out_9), .out_12(out_8),
    .out_13(out_7));
  Transistor #(.\type ("n"), .width(5)) transistor_11 (.in(5'b00100), .out(out_3), .gate(L));
  Transistor #(.\type ("n"), .width(5)) transistor_12 (.in(5'b01110), .out(out_4), .gate(L));
  Transistor #(.width(5)) transistor_13 (.in({5{1'b0}}), .out(out_3), .gate(L));
  Transistor #(.width(5)) transistor_14 (.in({5{1'b0}}), .out(out_5), .gate(L));
  Transistor #(.width(5)) transistor_15 (.in({5{1'b0}}), .out(out_4), .gate(L));
  or or_3 (R, in_1[0], in_1[1], in_1[2], in_1[3], in_1[4], in_1[5], in_1[6], in_1[7], in_1[8], in_1[9]);

  assign out_6 = {5{1'b0}};
  assign out_18 = {5{1'b0}};
  assign out_22 = in_2;
  assign out_23 = in_1;

  // Other names for the same wires on the sheet: _10_r = in_1[10]; _11_r = in_1[11]; L1[4:0] = out_5; L2[4:0] = out_4;
  //   L3[4:0] = out_3; _10_l = in_2[10]; _11_l = in_2[11]; R1[4:0] = out_21; R2[4:0] = out_20; R3[4:0] = out_19
endmodule

module otladka__v (
  input  [11:0] in_1,
  input  [11:0] in_2,
  output [4:0] out_3,
  output [4:0] out_4,
  output [4:0] out_5,
  output [4:0] out_6,
  output [4:0] out_7,
  output [4:0] out_8,
  output [4:0] out_9,
  output [4:0] out_10,
  output [4:0] out_11,
  output [4:0] out_12,
  output [4:0] out_13,
  output [4:0] out_14,
  output [4:0] out_15,
  output [4:0] out_16,
  output [4:0] out_17,
  output [4:0] out_18,
  output [4:0] out_19,
  output [4:0] out_20,
  output [4:0] out_21,
  output [11:0] out_22,
  output [11:0] out_23
);

  wire L, or_2_out, R;
  wire [9:0] transistor_4_out;

  Transistor #(.\type ("n"), .width(5)) transistor_1 (.in(5'b00111), .out(out_19), .gate(R));
  Transistor #(.\type ("n"), .width(5)) transistor_2 (.in(5'b00111), .out(out_21), .gate(R));
  Transistor #(.\type ("n"), .width(5)) transistor_3 (.in(5'b11100), .out(out_20), .gate(R));
  or or_1 (L, in_2[0], in_2[1], in_2[2], in_2[3], in_2[4], in_2[5], in_2[6], in_2[7], in_2[8], in_2[9]);
  Transistor #(.\type ("n"), .width(10)) transistor_4 (.in(in_2[9:0]), .out(transistor_4_out), .gate(L));
  or or_2 (or_2_out, R, L);
  Transistor #(.width(5)) transistor_5 (.in({5{1'b0}}), .out(out_20), .gate(R));
  Transistor #(.width(5)) transistor_6 (.in({5{1'b0}}), .out(out_21), .gate(R));
  Transistor #(.width(10)) transistor_7 (.in({10{1'b0}}), .out(transistor_4_out), .gate(or_2_out));
  Transistor #(.width(5)) transistor_8 (.in({5{1'b0}}), .out(out_19), .gate(R));
  Transistor #(.\type ("n"), .width(10)) transistor_9 (.in(in_1[9:0]), .out(transistor_4_out), .gate(R));
  DotMatrix #(.matrixcols(19), .matrixrows(5)) dotmatrix_1 (
    .col0(out_21), .col1(out_20), .col2(out_19), .col3({5{1'b0}}), .col4(out_17), .col5(out_16),
    .col6(out_15), .col7(out_14), .col8(out_13), .col9(out_12), .col10(out_11), .col11(out_10),
    .col12(out_9), .col13(out_8), .col14(out_7), .col15({5{1'b0}}), .col16(out_5), .col17(out_4),
    .col18(out_3));
  Transistor #(.\type ("n"), .width(5)) transistor_10 (.in(5'b11100), .out(out_5), .gate(L));
  Numders numders_1 (
    .Energy(transistor_4_out), .in_2(1'b0), .out_3(out_17), .out_4(out_16), .out_5(out_15), .out_6(out_14),
    .out_7(out_13), .out_8(out_12), .out_9(out_11), .out_10(out_10), .out_11(out_9), .out_12(out_8),
    .out_13(out_7));
  Transistor #(.\type ("n"), .width(5)) transistor_11 (.in(5'b11100), .out(out_3), .gate(L));
  Transistor #(.\type ("n"), .width(5)) transistor_12 (.in(5'b00111), .out(out_4), .gate(L));
  Transistor #(.width(5)) transistor_13 (.in({5{1'b0}}), .out(out_5), .gate(L));
  Transistor #(.width(5)) transistor_14 (.in({5{1'b0}}), .out(out_3), .gate(L));
  Transistor #(.width(5)) transistor_15 (.in({5{1'b0}}), .out(out_4), .gate(L));
  or or_3 (R, in_1[0], in_1[1], in_1[2], in_1[3], in_1[4], in_1[5], in_1[6], in_1[7], in_1[8], in_1[9]);

  assign out_6 = {5{1'b0}};
  assign out_18 = {5{1'b0}};
  assign out_22 = in_2;
  assign out_23 = in_1;

  // Other names for the same wires on the sheet: _10_l = in_2[10]; _11_l = in_2[11]; L1[4:0] = out_5; L2[4:0] = out_4;
  //   L3[4:0] = out_3; _10_r = in_1[10]; _11_r = in_1[11]; R1[4:0] = out_21; R2[4:0] = out_20; R3[4:0] = out_19
endmodule

module inc (
  input  [1:0] in_1,
  output [2:0] out_2
);

  wire [0:0] and_1_out;

  assign {out_2[2], and_1_out[0]} = {and_1_out[0], 1'b1} & in_1;  // AND_Gate and_1, 2 bits wide
  assign out_2[1:0] = in_1 ^ {and_1_out[0], 1'b1};  // XOR_Gate xor_1, 2 bits wide
endmodule
