// Logisim project people_controller.circ as structural Verilog: 1 circuit, main circuit main
module main (
  input  in_1,
  input  in_2,
  output [4:0] out_3
);

  wire [15:0] input_shifter_1_data_out;

  input_shifter input_shifter_1 (
    .MOSI(in_2), .CLK(in_1), .Data_out(input_shifter_1_data_out));  // open: Reset, buffer_ptr
endmodule
